// Logisim project 3_2.circ as structural Verilog: 1 circuit, main circuit main
module main (
  input  in_1,
  input  in_2,
  input  in_3,
  input  in_4,
  input  in_5,
  output \число___21 
);

  wire and_1_out, or_1_out, or_2_out;

  and and_1 (and_1_out, in_1, or_1_out);
  or or_1 (or_1_out, in_2, in_3);
  or or_2 (or_2_out, in_2, in_4);
  and and_2 (\число___21 , and_1_out, or_2_out);

  // Notes on the sheet:
  //   Вариант 9
endmodule
