// Logisim project 3_3.circ as structural Verilog: 1 circuit, main circuit main
module main (
  input  [3:0] in_1,
  input  [3:0] in_2,
  output [3:0] out_3,
  output \симметричность 
);

  wire xnor_1_out, xnor_2_out;

  Divider #(.width(4)) divider_1 (.a(in_1), .b(in_2), .rem(out_3));  // open: out, upper
  xnor xnor_1 (xnor_1_out, in_1[0], in_1[3]);
  xnor xnor_2 (xnor_2_out, in_1[2], in_1[1]);
  and and_1 (\симметричность , xnor_1_out, xnor_2_out);

  // Notes on the sheet:
  //   ввод
  //   остаток от деления
endmodule
