// Logisim project 2.circ as structural Verilog: 1 circuit, main circuit main
module main (
  input  in_1,
  input  in_2,
  input  in_3,
  output out_4,
  output out_5
);

  wire nand_1_out, nand_2_out, nand_3_out;

  nand nand_1 (nand_1_out, in_2, in_3);
  nand nand_2 (nand_2_out, in_1, nand_1_out);
  nand nand_3 (nand_3_out, nand_2_out, nand_1_out);
  nand nand_4 (out_4, nand_2_out, out_5);
  nand nand_5 (out_5, out_4, nand_3_out);
endmodule
