// Logisim project 1.circ as structural Verilog: 4 circuits, main circuit main
// схема сравнения
module main (
  input  in_1,
  input  in_2,
  output out_3
);

  wire and_1_out, and_2_out, not_1_out, not_2_out;

  not not_1 (not_1_out, in_1);
  not not_2 (not_2_out, in_2);
  and and_1 (and_1_out, not_1_out, in_2);
  and and_2 (and_2_out, in_1, not_2_out);
  or or_1 (out_3, and_1_out, and_2_out);
endmodule

module \полусумматор  (
  input  in_1,
  input  in_2,
  output out_3,
  output out_4
);

  wire and_2_out, and_3_out, not_1_out, not_2_out;

  not not_1 (not_1_out, in_1);
  not not_2 (not_2_out, in_2);
  and and_1 (out_3, in_1, in_2);
  and and_2 (and_2_out, not_1_out, in_2);
  and and_3 (and_3_out, in_1, not_2_out);
  or or_1 (out_4, and_2_out, and_3_out);
endmodule

module \полный_сумматор  (
  input  in_1,
  input  in_2,
  input  in_3,
  output out_4,
  output out_5
);

  wire \полусумматор_2_out_3 , \полусумматор_out_3 , \полусумматор_out_4 ;

  \полусумматор  \u_полусумматор  (
    .in_1(in_1), .in_2(in_2), .out_3(\полусумматор_out_3 ), .out_4(\полусумматор_out_4 ));
  \полусумматор  \u_полусумматор_2  (
    .in_1(\полусумматор_out_4 ), .in_2(in_3), .out_3(\полусумматор_2_out_3 ), .out_4(out_5));
  or or_1 (out_4, \полусумматор_out_3 , \полусумматор_2_out_3 );
endmodule

module \_4_сумматора  (
  input  in_1,
  input  in_2,
  input  in_3,
  input  in_4,
  input  in_5,
  input  in_6,
  input  in_7,
  input  in_8,
  input  in_9,
  output out_10,
  output out_11,
  output out_12,
  output out_13,
  output out_14
);

  wire \полный_сумматор_1_out_4 , \полный_сумматор_2_out_4 , \полный_сумматор_3_out_4 ;

  \полный_сумматор  \u_полный_сумматор_1  (
    .in_1(in_7), .in_2(in_8), .in_3(in_9), .out_4(\полный_сумматор_1_out_4 ), .out_5(out_14));
  \полный_сумматор  \u_полный_сумматор_2  (
    .in_1(in_3), .in_2(in_4), .in_3(\полный_сумматор_3_out_4 ), .out_4(\полный_сумматор_2_out_4 ),
    .out_5(out_12));
  \полный_сумматор  \u_полный_сумматор_3  (
    .in_1(in_5), .in_2(in_6), .in_3(\полный_сумматор_1_out_4 ), .out_4(\полный_сумматор_3_out_4 ),
    .out_5(out_13));
  \полный_сумматор  \u_полный_сумматор_4  (
    .in_1(in_1), .in_2(in_2), .in_3(\полный_сумматор_2_out_4 ), .out_4(out_10), .out_5(out_11));
endmodule
