// Logisim project 1.circ as structural Verilog: 1 circuit, main circuit main
module main (
  input  in_1,
  input  in_2,
  output out_3,
  output out_4
);

  nor nor_1 (out_3, in_1, out_4);
  nor nor_2 (out_4, out_3, in_2);

  // Notes on the sheet:
  //   асинхронный rs триггер с прямыми входами
endmodule
